# Fritzing sketch shield_baba (saved by Fritzing 0.6.3b)
breadboards: 1

parts:
  R1 = Resistor [tolerance=±5% resistance=10k package=THT]
  R2 = Resistor [tolerance=±5% resistance=10k package=THT]
  R3 = Resistor [tolerance=±5% resistance=22k package=THT]
  J1 = female pin header, 2 pins [form="♂ (male)"]
  J2 = female pin header, 2 pins [form="♂ (male)"]
  Q1 = NPN-Transistor [part_number=2n2222 package="SOT-23 [SMD]"]
  V_servo = Screw terminal - 2 pins [package=THT]
  C1 = Electrolytic Capacitor [capacitance=47µF voltage=35V package="100 mil [THT, electrolytic]"]
  C2 = Electrolytic Capacitor [capacitance=1µF package="100 mil [THT, electrolytic]"]
  U1 = Voltage Regulator - 5V [part_number=7805 package="TO220 [THT]"]
  J3 = female pin header, 7 pins [form="♀ (female)"]
  V_in = Screw terminal - 2 pins [package=THT]
  Baba_shield_Vers_0_3 = Arduino Ethernet Shield

nets:
  N1: R1.Pin_0, Baba_shield_Vers_0_3.D8
  N2: R1.Pin_1, Q1.0
  N3: R2.Pin_0, R3.Pin_0, Baba_shield_Vers_0_3.A5
  N4: R2.Pin_1, V_servo.pin2, C1.-, C2.-, U1.GND, V_in.pin2
  N5: R3.Pin_1, C1.+, U1.input_voltage, V_in.pin1
  N6: J1.pin1, J2.pin1, Q1.1
  N7: J1.pin2, J2.pin2, V_servo.pin1, C2.+, U1.output_voltage
  N8: Q1.2, Baba_shield_Vers_0_3.GND#1
  N9: J3.pin3, Baba_shield_Vers_0_3.D1TX
  N10: J3.pin4, Baba_shield_Vers_0_3.D0RX
  N11: J3.pin6, Baba_shield_Vers_0_3.+5V
  N12: J3.pin7, Baba_shield_Vers_0_3.GND#19
