# Fritzing sketch shield_romeo (saved by Fritzing 0.6.3b)
breadboards: 1

parts:
  Arduino1 = Arduino
  R1 = Resistor [tolerance=±5% resistance=1k package=THT]
  R2 = Resistor [tolerance=±5% resistance=2.2k package=THT]
  J2 = Screw terminal - 2 pins [part_number=Puissance_servo package=THT]
  C1 = Electrolytic Capacitor [capacitance=47µF voltage=35V package="100 mil [THT, electrolytic]"]
  C2 = Electrolytic Capacitor [capacitance=1µF package="100 mil [THT, electrolytic]"]
  C3 = Electrolytic Capacitor [capacitance=1µF package="100 mil [THT, electrolytic]"]
  C4 = Electrolytic Capacitor [capacitance=47µF voltage=35V package="100 mil [THT, electrolytic]"]
  U2 = Voltage Regulator - Variable [package="TO220 [THT]"]
  U3 = Voltage Regulator - 5V [package="TO220 [THT]"]
  J3 = Screw terminal - 2 pins [part_number=V_alim package=THT]
  Q1 = NPN-Transistor [package="TO92 [THT]"]
  R3 = Resistor [tolerance=±5% resistance=1k package=THT]
  R4 = Resistor [tolerance=±5% resistance=1k package=THT]
  Q2 = NPN-Transistor [package="TO92 [THT]"]
  J4 = female pin header, 2 pins [form="♂ (male)" part_number=Eclairage_gauche]
  J5 = female pin header, 2 pins [form="♂ (male)" part_number=Eclairage_droite]

nets:
  GND: Arduino1.GND, R1.Pin_1, J2.pin2, C1.-, C2.-, C3.-, C4.-, U2.ADJ, U3.GND, J3.pin1, Q1.E, Q2.E
  N1: Arduino1.D13, R3.Pin_1
  N2: Arduino1.D12, R4.Pin_1
  5V: Arduino1.+5V
  N3: Arduino1.A1, R1.Pin_0, R2.Pin_1
  N4: R2.Pin_0, C1.+, C4.+, U2.IN, U3.input_voltage, J3.pin2
  N5: J2.pin1, C2.+, U3.output_voltage
  N6: C3.+, U2.OUT, J4.pin1, J5.pin1
  N7: Q1.B, R3.Pin_0
  N8: Q1.C, J4.pin2
  N9: R4.Pin_0, Q2.B
  N10: Q2.C, J5.pin2
