# Fritzing sketch shield_romeo_v_0_2_1 (saved by Fritzing 0.6.3b)
breadboards: 1

parts:
  C1 = Electrolytic Capacitor [capacitance=0.47mF package="100 mil [THT, electrolytic]"]
  C2 = Electrolytic Capacitor [capacitance=1µF package="100 mil [THT, electrolytic]"]
  U1 = Voltage Regulator - 5V [package="TO220 [THT]"]
  R1 = Resistor [tolerance=±5% resistance=10k package=THT]
  R2 = Resistor [tolerance=±5% resistance=220 package=THT]
  R3 = Resistor [tolerance=±5% resistance=220 package=THT]
  J4 = female pin header, 2 pins [form="♂ (male)"]
  J3 = female pin header, 2 pins [form="♂ (male)"]
  U3 = Voltage Regulator - 5V [package="TO220 [THT]"]
  C3 = Electrolytic Capacitor [capacitance=1µF package="100 mil [THT, electrolytic]"]
  C4 = Electrolytic Capacitor [capacitance=1µF package="100 mil [THT, electrolytic]"]
  Arduino_Ethernet_Shield1 = Arduino Ethernet Shield
  Q1 = NPN-Transistor [package="SOT-23 [SMD]"]
  V_servo = Screw terminal - 2 pins [package=THT]
  V_in = Screw terminal - 2 pins [package=THT]

nets:
  GND: C1.-, C2.-, U1.GND, R2.Pin_1, U3.GND, C3.-, C4.-, V_servo.pin2, V_in.pin2
  N1: C1.+, U1.input_voltage, R3.Pin_1, U3.input_voltage, C3.+, V_in.pin1
  N2: C2.+, U1.output_voltage, V_servo.pin1
  N3: R1.Pin_0, Arduino_Ethernet_Shield1.D8
  N4: R1.Pin_1, Q1.0
  N5: R2.Pin_0, R3.Pin_0, Arduino_Ethernet_Shield1.A5
  N6: J4.pin1, J3.pin1, Q1.1
  N7: J4.pin2, J3.pin2, U3.output_voltage, C4.+
  N8: Arduino_Ethernet_Shield1.GND, Q1.2
